# Fritzing sketch fridge (saved by Fritzing 1.0.1rc)
breadboards: 1

parts:
  Mod1 = Raspberry Pi Pico W
  S1 = MC-38
  buz1 = Piezo Buzzer
  DS1 = DS18B20 1-Wire Temperature Sensor [part_number=DS18B20]
  R1 = Resistor [tolerance=±5% resistance=2.2k package="0603 [SMD]"]

nets:
  N1: Mod1.pin_3, Mod1.pin_8, Mod1.pin_13, Mod1.pin_18, Mod1.pin_23, Mod1.pin_28, Mod1.pin_33, Mod1.pin_38, Mod1.pin_42, S1.pin_2, buz1.pin_2, DS1.GND
  N2: Mod1.pin_19, S1.pin_1
  N3: Mod1.pin_20, buz1.pin_1
  N4: Mod1.pin_29, DS1.DQ, R1.Pin_1
  N5: Mod1.pin_36, DS1.VDD, R1.Pin_0

notes:
  MC-38 Sensor

custom parts:
  Raspberry Pi Pico W: Raspberry Pi Pico W. Based around the RP2040 microcontroller the Pico W is a low cost microcontroller device bringing Raspberry Pi quality, cost, and easy of use to the microcontroller space. The areas marked KEEPOUT in pcb silkscreen should not have traces running through them to avoid shorts on a soldered in module!
  MC-38: MC-38 Contact Sensor w/ Reed Switch
  Piezo Buzzer: Part from https://www.nutsvolts.com/magazine/article/november2012_SmileysWorkshop. Breadboard and icon images modified to be 0.3" in spacing and be more similar to the actual physical part.
